// Logisim project CPU.circ as structural Verilog: 8 circuits, main circuit main
module main (
  input  in_1,
  input  in_2,
  input  in_3,
  input  in_4,
  input  in_5,
  input  in_6,
  input  in_7,
  input  in_8,
  input  in_9,
  input  Enable,
  input  Enable_2,
  output out_12
);

  wire Clock_2_clock_status, Clock_2_value, Clock_out, Clock_Select_out, Halt_out, Register__0_2,
       Register__0_3, Register__0_4, Register__0_5, Register__0_6, Register__0_7, Register__0_8,
       Register__0_9, Step_out, Step_Select_out;

  Clock_part Clock (.out(Clock_out));
  Button Clock_Select (.out(Clock_Select_out));
  Button Step_Select (.out(Step_Select_out));
  LED Clock_Status (.in(Clock_2_clock_status));
  Button Step (.out(Step_out));
  Button Halt (.out(Halt_out));
  Register Register (
    .CLK(Clock_2_value), .Load(Enable), ._0(Register__0_2), ._1(Register__0_3), ._2(Register__0_4),
    ._3(Register__0_5), ._4(Register__0_6), ._5(Register__0_7), ._6(Register__0_8), ._7(Register__0_9),
    .Enable(Enable_2), ._0_2(Register__0_2), ._0_3(Register__0_3), ._0_4(Register__0_4),
    ._0_5(Register__0_5), ._0_6(Register__0_6), ._0_7(Register__0_7), ._0_8(Register__0_8),
    ._0_9(Register__0_9));
  LED Clock_Throughput (.in(Clock_2_value));
  Clock Clock_2 (
    .Clock(Clock_out), .Clock_Select(Clock_Select_out), .Clock_Status(Clock_2_clock_status),
    .Step_Select(Step_Select_out), .Halt(Halt_out), .Step(Step_out), .Value(Clock_2_value));
  assign Register__0_3 = in_9 ? in_2 : 1'bz;  // Controlled_Buffer controlled_buffer_1
  assign Register__0_2 = in_9 ? in_1 : 1'bz;  // Controlled_Buffer controlled_buffer_2
  assign Register__0_7 = in_9 ? in_6 : 1'bz;  // Controlled_Buffer controlled_buffer_3
  assign Register__0_4 = in_9 ? in_3 : 1'bz;  // Controlled_Buffer controlled_buffer_4
  assign Register__0_5 = in_9 ? in_4 : 1'bz;  // Controlled_Buffer controlled_buffer_5
  assign Register__0_6 = in_9 ? in_5 : 1'bz;  // Controlled_Buffer controlled_buffer_6
  assign Register__0_8 = in_9 ? in_7 : 1'bz;  // Controlled_Buffer controlled_buffer_7
  assign Register__0_9 = in_9 ? in_8 : 1'bz;  // Controlled_Buffer controlled_buffer_8
endmodule

module Clock (
  input  Clock,
  input  Clock_Select,
  input  Step_Select,
  input  Halt,
  input  Step,
  output Clock_Status,
  output Value
);

  wire and_1_out, and_2_out, not_2_out, or_1_out, Switch_q;

  Switch Switch (.in_1(Clock_Select), .in_2(or_1_out), .Q(Switch_q));
  or or_1 (or_1_out, Step_Select, Halt);
  not not_1 (Clock_Status, Switch_q);
  and and_1 (and_1_out, Clock, Clock_Status);
  and and_2 (and_2_out, Step, not_2_out);
  not not_2 (not_2_out, Clock_Status);
  or or_2 (Value, and_1_out, and_2_out);

  // Notes on the sheet:
  //   1 = ON, 0 = OFF
  //   When Step is triggered, it will
  //   advance the clock 1 tick
endmodule

module Switch_2 (
  input  Switch_Toggle,
  output Switch_Value
);

  wire button_1_out, d_ff_1_qn;

  Button button_1 (.out(button_1_out));
  D_Flip_Flop_part d_ff_1 (
    .clk(button_1_out), .D(d_ff_1_qn), .Q(Switch_Value), .Qn(d_ff_1_qn));  // open: preset, en, reset
endmodule

module D_Flip_Flop (
  input  CLK,
  input  D,
  output Q,
  output nQ
);

  wire and_1_out, and_2_out, not_1_out;

  not not_1 (not_1_out, D);
  and and_1 (and_1_out, not_1_out, CLK);
  and and_2 (and_2_out, CLK, D);
  nor nor_1 (Q, and_1_out, nQ);
  nor nor_2 (nQ, Q, and_2_out);
endmodule

module SR_Latch (
  input  in_1,
  input  in_2,
  output Q,
  output nQ
);

  nor nor_1 (Q, in_1, nQ);
  nor nor_2 (nQ, Q, in_2);
endmodule

module Switch (
  input  in_1,
  input  in_2,
  output Q
);

  SR_Latch SR_Latch (.in_1(in_1), .in_2(in_2), .Q(Q));  // open: nQ
endmodule

module Register (
  input  CLK,
  input  Load,
  input  _0,
  input  _1,
  input  _2,
  input  _3,
  input  _4,
  input  _5,
  input  _6,
  input  _7,
  input  Enable,
  output _0_2,
  output _0_3,
  output _0_4,
  output _0_5,
  output _0_6,
  output _0_7,
  output _0_8,
  output _0_9
);

  wire _1_Bit_Register_2_output, _1_Bit_Register_3_output, _1_Bit_Register_4_output,
       _1_Bit_Register_5_output, _1_Bit_Register_6_output, _1_Bit_Register_7_output,
       _1_Bit_Register_8_output, _1_Bit_Register_output;

  _1_Bit_Register _1_Bit_Register (.CLK(CLK), .Load(Load), .Data(_0), .Output(_1_Bit_Register_output));
  _1_Bit_Register _1_Bit_Register_2 (.CLK(CLK), .Load(Load), .Data(_1), .Output(_1_Bit_Register_2_output));
  _1_Bit_Register _1_Bit_Register_3 (.CLK(CLK), .Load(Load), .Data(_2), .Output(_1_Bit_Register_3_output));
  _1_Bit_Register _1_Bit_Register_4 (.CLK(CLK), .Load(Load), .Data(_3), .Output(_1_Bit_Register_4_output));
  _1_Bit_Register _1_Bit_Register_5 (.CLK(CLK), .Load(Load), .Data(_4), .Output(_1_Bit_Register_5_output));
  _1_Bit_Register _1_Bit_Register_6 (.CLK(CLK), .Load(Load), .Data(_5), .Output(_1_Bit_Register_6_output));
  _1_Bit_Register _1_Bit_Register_7 (.CLK(CLK), .Load(Load), .Data(_6), .Output(_1_Bit_Register_7_output));
  _1_Bit_Register _1_Bit_Register_8 (.CLK(CLK), .Load(Load), .Data(_7), .Output(_1_Bit_Register_8_output));
  assign _0_2 = Enable ? _1_Bit_Register_output : 1'bz;  // Controlled_Buffer controlled_buffer_1
  assign _0_3 = Enable ? _1_Bit_Register_2_output : 1'bz;  // Controlled_Buffer controlled_buffer_2
  assign _0_4 = Enable ? _1_Bit_Register_3_output : 1'bz;  // Controlled_Buffer controlled_buffer_3
  assign _0_5 = Enable ? _1_Bit_Register_4_output : 1'bz;  // Controlled_Buffer controlled_buffer_4
  assign _0_7 = Enable ? _1_Bit_Register_6_output : 1'bz;  // Controlled_Buffer controlled_buffer_5
  assign _0_6 = Enable ? _1_Bit_Register_5_output : 1'bz;  // Controlled_Buffer controlled_buffer_6
  assign _0_8 = Enable ? _1_Bit_Register_7_output : 1'bz;  // Controlled_Buffer controlled_buffer_7
  assign _0_9 = Enable ? _1_Bit_Register_8_output : 1'bz;  // Controlled_Buffer controlled_buffer_8
endmodule

module _1_Bit_Register (
  input  CLK,
  input  Load,
  input  Data,
  output Output
);

  wire and_1_out, and_2_out, controlled_buffer_1_out, not_1_out, or_1_out;

  assign controlled_buffer_1_out = Load ? Data : 1'bz;  // Controlled_Buffer controlled_buffer_1
  not not_1 (not_1_out, Load);
  and and_1 (and_1_out, Load, controlled_buffer_1_out);
  or or_1 (or_1_out, and_1_out, and_2_out);
  and and_2 (and_2_out, not_1_out, Output);
  D_Flip_Flop_part d_ff_1 (.clk(CLK), .D(or_1_out), .Q(Output));  // open: Qn, preset, en, reset
endmodule
