// Logisim project CPU1.circ as structural Verilog: 10 circuits, main circuit main
module main (
  input  in_1,
  input  in_2,
  input  in_3,
  input  in_4,
  input  in_5,
  input  in_6,
  input  in_7,
  input  in_8,
  input  in_9,
  input  Input,
  input  Output,
  input  Input_2,
  input  Output_2,
  output out_14
);

  wire Clock_2_clock_status, Clock_2_value, Clock_out, Clock_Select_out, Halt_out, Register_2_out_12,
       Register_2_out_13, Register_2_out_14, Register_2_out_15, Register_2_out_16, Register_2_out_17,
       Register_2_out_18, Register_2_out_19, Register_out_12, Register_out_13, Register_out_14,
       Register_out_15, Register_out_16, Register_out_17, Register_out_18, Register_out_19, Step_out,
       Step_Select_out;
  wire [7:0] Register__0_2;

  Clock_part Clock (.out(Clock_out));
  Button Clock_Select (.out(Clock_Select_out));
  Button Step_Select (.out(Step_Select_out));
  LED Clock_Status (.in(Clock_2_clock_status));
  Button Step (.out(Step_out));
  Button Halt (.out(Halt_out));
  Register Register (
    .CLK(Clock_2_value), .Load(Input), ._0(Register__0_2[0]), ._1(Register__0_2[1]), ._2(Register__0_2[2]),
    ._3(Register__0_2[3]), ._4(Register__0_2[4]), ._5(Register__0_2[5]), ._6(Register__0_2[6]),
    ._7(Register__0_2[7]), .Enable(Output), .out_12(Register_out_12), .out_13(Register_out_13),
    .out_14(Register_out_14), .out_15(Register_out_15), .out_16(Register_out_16), .out_17(Register_out_17),
    .out_18(Register_out_18), .out_19(Register_out_19), ._0_2(Register__0_2));
  DotMatrix #(.matrixcols(8), .matrixrows(1)) dotmatrix_1 (
    .col0(Register_out_12), .col1(Register_out_13), .col2(Register_out_14), .col3(Register_out_15),
    .col4(Register_out_16), .col5(Register_out_17), .col6(Register_out_18), .col7(Register_out_19));
  Register Register_2 (
    .CLK(Clock_2_value), .Load(Input_2), ._0(Register__0_2[0]), ._1(Register__0_2[1]), ._2(Register__0_2[2]),
    ._3(Register__0_2[3]), ._4(Register__0_2[4]), ._5(Register__0_2[5]), ._6(Register__0_2[6]),
    ._7(Register__0_2[7]), .Enable(Output_2), .out_12(Register_2_out_12), .out_13(Register_2_out_13),
    .out_14(Register_2_out_14), .out_15(Register_2_out_15), .out_16(Register_2_out_16),
    .out_17(Register_2_out_17), .out_18(Register_2_out_18), .out_19(Register_2_out_19), ._0_2(Register__0_2));
  DotMatrix #(.matrixcols(8), .matrixrows(1)) dotmatrix_2 (
    .col0(Register_2_out_12), .col1(Register_2_out_13), .col2(Register_2_out_14), .col3(Register_2_out_15),
    .col4(Register_2_out_16), .col5(Register_2_out_17), .col6(Register_2_out_18), .col7(Register_2_out_19));
  LED Throughput (.in(Clock_2_value));
  Clock Clock_2 (
    .Clock(Clock_out), .Clock_Select(Clock_Select_out), .Clock_Status(Clock_2_clock_status),
    .Step_Select(Step_Select_out), .Halt(Halt_out), .Step(Step_out), .Value(Clock_2_value));
  assign Register__0_2[1] = in_9 ? in_2 : 1'bz;  // Controlled_Buffer controlled_buffer_1
  assign Register__0_2[0] = in_9 ? in_1 : 1'bz;  // Controlled_Buffer controlled_buffer_2
  Pull_Resistor pull_resistor_1 (.node(Register__0_2[1]));
  Pull_Resistor pull_resistor_2 (.node(Register__0_2[0]));
  assign Register__0_2[4] = in_9 ? in_5 : 1'bz;  // Controlled_Buffer controlled_buffer_3
  assign Register__0_2[2] = in_9 ? in_3 : 1'bz;  // Controlled_Buffer controlled_buffer_4
  assign Register__0_2[5] = in_9 ? in_6 : 1'bz;  // Controlled_Buffer controlled_buffer_5
  assign Register__0_2[3] = in_9 ? in_4 : 1'bz;  // Controlled_Buffer controlled_buffer_6
  Pull_Resistor pull_resistor_3 (.node(Register__0_2[3]));
  Pull_Resistor pull_resistor_4 (.node(Register__0_2[2]));
  Pull_Resistor pull_resistor_5 (.node(Register__0_2[4]));
  Pull_Resistor pull_resistor_6 (.node(Register__0_2[5]));
  assign Register__0_2[7] = in_9 ? in_8 : 1'bz;  // Controlled_Buffer controlled_buffer_7
  assign Register__0_2[6] = in_9 ? in_7 : 1'bz;  // Controlled_Buffer controlled_buffer_8
  Pull_Resistor pull_resistor_7 (.node(Register__0_2[6]));
  Pull_Resistor pull_resistor_8 (.node(Register__0_2[7]));
endmodule

module Clock (
  input  Clock,
  input  Clock_Select,
  input  Step_Select,
  input  Halt,
  input  Step,
  output Clock_Status,
  output Value
);

  wire and_1_out, and_2_out, not_2_out, or_1_out, Switch_q;

  Switch Switch (.in_1(Clock_Select), .in_2(or_1_out), .Q(Switch_q));
  or or_1 (or_1_out, Step_Select, Halt);
  not not_1 (Clock_Status, Switch_q);
  and and_1 (and_1_out, Clock, Clock_Status);
  and and_2 (and_2_out, Step, not_2_out);
  not not_2 (not_2_out, Clock_Status);
  or or_2 (Value, and_1_out, and_2_out);

  // Notes on the sheet:
  //   1 = ON, 0 = OFF
  //   When Step is triggered, it will
  //   advance the clock 1 tick
endmodule

module Switch_2 (
  input  Switch_Toggle,
  output Switch_Value
);

  wire button_1_out, d_ff_1_qn;

  Button button_1 (.out(button_1_out));
  D_Flip_Flop_part d_ff_1 (
    .clk(button_1_out), .D(d_ff_1_qn), .Q(Switch_Value), .Qn(d_ff_1_qn));  // open: preset, en, reset
endmodule

module D_Flip_Flop (
  input  CLK,
  input  D,
  output Q,
  output nQ
);

  wire and_1_out, and_2_out, not_1_out;

  not not_1 (not_1_out, D);
  and and_1 (and_1_out, not_1_out, CLK);
  and and_2 (and_2_out, CLK, D);
  nor nor_1 (Q, and_1_out, nQ);
  nor nor_2 (nQ, Q, and_2_out);
endmodule

module SR_Latch (
  input  in_1,
  input  in_2,
  output Q,
  output nQ
);

  nor nor_1 (Q, in_1, nQ);
  nor nor_2 (nQ, Q, in_2);
endmodule

module Switch (
  input  in_1,
  input  in_2,
  output Q
);

  SR_Latch SR_Latch (.in_1(in_1), .in_2(in_2), .Q(Q));  // open: nQ
endmodule

module Register (
  input  CLK,
  input  Load,
  input  _0,
  input  _1,
  input  _2,
  input  _3,
  input  _4,
  input  _5,
  input  _6,
  input  _7,
  input  Enable,
  output out_12,
  output out_13,
  output out_14,
  output out_15,
  output out_16,
  output out_17,
  output out_18,
  output out_19,
  output [7:0] _0_2
);

  _1_Bit_Register _1_Bit_Register (.CLK(CLK), .Load(Load), .Data(_0), .Output(out_12));
  _1_Bit_Register _1_Bit_Register_2 (.CLK(CLK), .Load(Load), .Data(_1), .Output(out_13));
  _1_Bit_Register _1_Bit_Register_3 (.CLK(CLK), .Load(Load), .Data(_2), .Output(out_14));
  _1_Bit_Register _1_Bit_Register_4 (.CLK(CLK), .Load(Load), .Data(_3), .Output(out_15));
  _1_Bit_Register _1_Bit_Register_5 (.CLK(CLK), .Load(Load), .Data(_4), .Output(out_16));
  _1_Bit_Register _1_Bit_Register_6 (.CLK(CLK), .Load(Load), .Data(_5), .Output(out_17));
  _1_Bit_Register _1_Bit_Register_7 (.CLK(CLK), .Load(Load), .Data(_6), .Output(out_18));
  _1_Bit_Register _1_Bit_Register_8 (.CLK(CLK), .Load(Load), .Data(_7), .Output(out_19));
  assign _0_2 = Enable ? {out_19, out_18, out_17, out_16, out_15, out_14, out_13, out_12} : 8'bz;  // Controlled_Buffer controlled_buffer_1
endmodule

module _1_Bit_Register (
  input  CLK,
  input  Load,
  input  Data,
  output Output
);

  wire and_1_out, and_2_out, controlled_buffer_1_out, not_1_out, or_1_out;

  assign controlled_buffer_1_out = Load ? Data : 1'bz;  // Controlled_Buffer controlled_buffer_1
  not not_1 (not_1_out, Load);
  and and_1 (and_1_out, Load, controlled_buffer_1_out);
  or or_1 (or_1_out, and_1_out, and_2_out);
  and and_2 (and_2_out, not_1_out, Output);
  D_Flip_Flop_part d_ff_1 (.clk(CLK), .D(or_1_out), .Q(Output));  // open: Qn, preset, en, reset
endmodule

module _1_Bit_Adder (
  input  Carry_In,
  input  A,
  input  B,
  output Sum,
  output Carry_Out
);

  wire and_1_out, and_2_out, and_3_out, and_4_out, and_5_out, and_6_out, and_7_out, and_8_out, not_1_out,
       not_2_out, not_3_out, not_4_out, not_5_out, not_6_out, not_7_out, not_8_out, not_9_out;

  not not_1 (not_1_out, A);
  not not_2 (not_2_out, B);
  not not_3 (not_3_out, A);
  not not_4 (not_4_out, Carry_In);
  not not_5 (not_5_out, B);
  not not_6 (not_6_out, Carry_In);
  not not_7 (not_7_out, A);
  not not_8 (not_8_out, B);
  not not_9 (not_9_out, Carry_In);
  and and_1 (and_1_out, not_1_out, not_2_out, Carry_In);
  and and_2 (and_2_out, not_3_out, B, not_4_out);
  and and_3 (and_3_out, A, not_5_out, not_6_out);
  and and_4 (and_4_out, A, B, Carry_In);
  and and_5 (and_5_out, not_7_out, B, Carry_In);
  and and_6 (and_6_out, A, not_8_out, Carry_In);
  and and_7 (and_7_out, A, B, not_9_out);
  and and_8 (and_8_out, A, B, Carry_In);
  or or_1 (Sum, and_1_out, and_2_out, and_3_out, and_4_out);
  or or_2 (Carry_Out, and_5_out, and_6_out, and_7_out, and_8_out);
  // OR_Gate or_3 is placed but not wired
endmodule

module Adder (
  input  A3,
  input  B3,
  input  A2,
  input  B2,
  input  A1,
  input  B1,
  input  A0,
  input  B0,
  output out_9,
  output out_10,
  output out_11,
  output out_12
);

  wire n1_bit_adder_2_carry_out, n1_bit_adder_3_carry_out, n1_bit_adder_4_carry_out;

  _1_Bit_Adder u_1_bit_adder_1 (.A(A3), .B(B3), .Sum(out_9), .Carry_In(n1_bit_adder_2_carry_out));  // open: Carry_Out
  _1_Bit_Adder u_1_bit_adder_2 (
    .Carry_Out(n1_bit_adder_2_carry_out), .A(A2), .B(B2), .Sum(out_10), .Carry_In(n1_bit_adder_3_carry_out));
  _1_Bit_Adder u_1_bit_adder_3 (
    .Carry_Out(n1_bit_adder_3_carry_out), .A(A1), .B(B1), .Sum(out_11), .Carry_In(n1_bit_adder_4_carry_out));
  _1_Bit_Adder u_1_bit_adder_4 (.Carry_Out(n1_bit_adder_4_carry_out), .A(A0), .B(B0), .Sum(out_12), .Carry_In(1'b0));
endmodule
