// Logisim project CPU2.circ as structural Verilog: 16 circuits, main circuit main
module main (
  input  Enable_Manual_Data,
  input  in_2,
  input  in_3,
  input  in_4,
  input  in_5,
  input  in_6,
  input  in_7,
  input  in_8,
  input  in_9,
  input  Jump,
  input  [3:0] Jump_Address,
  input  Enable,
  input  ALU_Register_1_Write,
  input  ALU_Register_2_Write,
  input  ALU_Enable,
  input  ALU_Subtract,
  input  RAM_Write_Enable,
  input  [3:0] RAM_Write_Select_Line,
  input  [3:0] RAM_Read_Select_Line,
  input  RAM_Read_Enable,
  output out_21
);

  wire ALU_A_Register__0_2, ALU_A_Register__1_2, ALU_A_Register__2_2, ALU_A_Register__3_2,
       ALU_A_Register__4_2, ALU_A_Register__5_2, ALU_A_Register__6_2, ALU_A_Register__7_2,
       ALU_B_Register__0_2, ALU_B_Register__1_2, ALU_B_Register__2_2, ALU_B_Register__3_2,
       ALU_B_Register__4_2, ALU_B_Register__5_2, ALU_B_Register__6_2, ALU_B_Register__7_2,
       Clock_2_clock_status, Clock_2_value, Clock_out, Clock_Select_out, program_2_add_loop_1__0,
       program_2_add_loop_1__0___halt_program, program_2_add_loop_1__1___write_alu_register_a,
       program_2_add_loop_1__2___write_alu_register_b, program_2_add_loop_1__3___alu_enable,
       program_2_add_loop_1__4___alu_subtract, program_2_add_loop_1__7, program_2_add_loop_1_out_4,
       program_2_add_loop_1_out_5, program_2_add_loop_1_out_6, program_2_add_loop_1_out_7,
       program_2_add_loop_1_out_8, program_2_add_loop_1_out_9, Step_out, Step_Select_out;
  wire [3:0] Program_Counter_out_8;
  wire [7:0] ALU_A_Register__8_bit_output, ALU_B_Register__8_bit_output;

  Clock_part Clock (.out(Clock_out));
  Button Clock_Select (.out(Clock_Select_out));
  Button Step_Select (.out(Step_Select_out));
  LED Clock_Status (.in(Clock_2_clock_status));
  Button Step (.out(Step_out));
  Clock Clock_2 (
    .Clock(Clock_out), .Clock_Select(Clock_Select_out), .Clock_Status(Clock_2_clock_status),
    .Step_Select(Step_Select_out), .Halt(program_2_add_loop_1__0___halt_program), .Step(Step_out),
    .Value(Clock_2_value));
  LED CLK_Throughput (.in(Clock_2_value));
  Program_Counter Program_Counter (
    .CLK(Clock_2_value), .Jump_Enable(Jump), .Enable(Enable), .out_5(Program_Counter_out_8[3]),
    .out_6(Program_Counter_out_8[2]), .out_7(Program_Counter_out_8[1]), .out_8(Program_Counter_out_8[0]),
    .Jump_Address(Jump_Address));
  DotMatrix #(.matrixcols(4), .matrixrows(1)) dotmatrix_1 (
    .col0(Program_Counter_out_8[3]), .col1(Program_Counter_out_8[2]), .col2(Program_Counter_out_8[1]),
    .col3(Program_Counter_out_8[0]));
  Program_2___Add_Loop program_2_add_loop_1 (
    .Read_Address(Program_Counter_out_8), .CLK(Clock_2_value),
    ._0___Halt_Program(program_2_add_loop_1__0___halt_program),
    ._1___Write_ALU_Register_A(program_2_add_loop_1__1___write_alu_register_a),
    ._2___Write_ALU_Register_B(program_2_add_loop_1__2___write_alu_register_b),
    ._3___ALU_Enable(program_2_add_loop_1__3___alu_enable),
    ._4___ALU_Subtract(program_2_add_loop_1__4___alu_subtract), ._0(program_2_add_loop_1__0),
    .out_4(program_2_add_loop_1_out_4), .out_5(program_2_add_loop_1_out_5),
    .out_6(program_2_add_loop_1_out_6), .out_7(program_2_add_loop_1_out_7),
    .out_8(program_2_add_loop_1_out_8), .out_9(program_2_add_loop_1_out_9), ._7(program_2_add_loop_1__7));
  assign program_2_add_loop_1__7 = Enable_Manual_Data ? in_2 : 1'bz;  // Controlled_Buffer controlled_buffer_1
  assign program_2_add_loop_1_out_9 = Enable_Manual_Data ? in_3 : 1'bz;  // Controlled_Buffer controlled_buffer_2
  Pull_Resistor pull_resistor_1 (.node(program_2_add_loop_1_out_9));
  Pull_Resistor pull_resistor_2 (.node(program_2_add_loop_1__7));
  LED led_1 (.in(program_2_add_loop_1_out_9));
  LED led_2 (.in(program_2_add_loop_1__7));
  assign program_2_add_loop_1_out_6 = Enable_Manual_Data ? in_6 : 1'bz;  // Controlled_Buffer controlled_buffer_3
  assign program_2_add_loop_1_out_5 = Enable_Manual_Data ? in_7 : 1'bz;  // Controlled_Buffer controlled_buffer_4
  assign program_2_add_loop_1_out_7 = Enable_Manual_Data ? in_5 : 1'bz;  // Controlled_Buffer controlled_buffer_5
  assign program_2_add_loop_1_out_8 = Enable_Manual_Data ? in_4 : 1'bz;  // Controlled_Buffer controlled_buffer_6
  Pull_Resistor pull_resistor_3 (.node(program_2_add_loop_1_out_6));
  Pull_Resistor pull_resistor_4 (.node(program_2_add_loop_1_out_5));
  Pull_Resistor pull_resistor_5 (.node(program_2_add_loop_1_out_8));
  Pull_Resistor pull_resistor_6 (.node(program_2_add_loop_1_out_7));
  LED led_3 (.in(program_2_add_loop_1_out_8));
  LED led_4 (.in(program_2_add_loop_1_out_5));
  LED led_5 (.in(program_2_add_loop_1_out_6));
  LED led_6 (.in(program_2_add_loop_1_out_7));
  assign program_2_add_loop_1_out_4 = Enable_Manual_Data ? in_8 : 1'bz;  // Controlled_Buffer controlled_buffer_7
  assign program_2_add_loop_1__0 = Enable_Manual_Data ? in_9 : 1'bz;  // Controlled_Buffer controlled_buffer_8
  Pull_Resistor pull_resistor_7 (.node(program_2_add_loop_1_out_4));
  Pull_Resistor pull_resistor_8 (.node(program_2_add_loop_1__0));
  LED led_7 (.in(program_2_add_loop_1_out_4));
  LED led_8 (.in(program_2_add_loop_1__0));
  _8_Bit_Register ALU_B_Register (
    .CLK(Clock_2_value), .Load(program_2_add_loop_1__2___write_alu_register_b), ._7(program_2_add_loop_1__7),
    ._6(program_2_add_loop_1_out_9), ._5(program_2_add_loop_1_out_8), ._4(program_2_add_loop_1_out_7),
    ._3(program_2_add_loop_1_out_6), ._2(program_2_add_loop_1_out_5), ._1(program_2_add_loop_1_out_4),
    ._0(program_2_add_loop_1__0), ._7_2(ALU_B_Register__7_2), ._6_2(ALU_B_Register__6_2),
    ._5_2(ALU_B_Register__5_2), ._4_2(ALU_B_Register__4_2), ._3_2(ALU_B_Register__3_2),
    ._2_2(ALU_B_Register__2_2), ._1_2(ALU_B_Register__1_2), ._0_2(ALU_B_Register__0_2),
    ._8_Bit_Output(ALU_B_Register__8_bit_output));
  DotMatrix #(.matrixcols(8), .matrixrows(1)) dotmatrix_2 (
    .col0(ALU_B_Register__7_2), .col1(ALU_B_Register__6_2), .col2(ALU_B_Register__5_2),
    .col3(ALU_B_Register__4_2), .col4(ALU_B_Register__3_2), .col5(ALU_B_Register__2_2),
    .col6(ALU_B_Register__1_2), .col7(ALU_B_Register__0_2));
  RAM RAM (
    .in_10(RAM_Write_Enable), .Write_Address(RAM_Write_Select_Line), .Read_Address(RAM_Read_Select_Line),
    .Read(RAM_Read_Enable), .CLK(Clock_2_value), .in_2(program_2_add_loop_1__7),
    .in_3(program_2_add_loop_1_out_9), .in_4(program_2_add_loop_1_out_8), .in_5(program_2_add_loop_1_out_7),
    .in_6(program_2_add_loop_1_out_6), .in_7(program_2_add_loop_1_out_5), .in_8(program_2_add_loop_1_out_4),
    .in_9(program_2_add_loop_1__0), .out_14(program_2_add_loop_1__7), .out_15(program_2_add_loop_1_out_9),
    .out_16(program_2_add_loop_1_out_8), .out_17(program_2_add_loop_1_out_7),
    .out_18(program_2_add_loop_1_out_6), .out_19(program_2_add_loop_1_out_5),
    .out_20(program_2_add_loop_1_out_4), .out_21(program_2_add_loop_1__0));
  _8_Bit_Register ALU_A_Register (
    .CLK(Clock_2_value), .Load(program_2_add_loop_1__1___write_alu_register_a), ._7(program_2_add_loop_1__7),
    ._6(program_2_add_loop_1_out_9), ._5(program_2_add_loop_1_out_8), ._4(program_2_add_loop_1_out_7),
    ._3(program_2_add_loop_1_out_6), ._2(program_2_add_loop_1_out_5), ._1(program_2_add_loop_1_out_4),
    ._0(program_2_add_loop_1__0), ._7_2(ALU_A_Register__7_2), ._6_2(ALU_A_Register__6_2),
    ._5_2(ALU_A_Register__5_2), ._4_2(ALU_A_Register__4_2), ._3_2(ALU_A_Register__3_2),
    ._2_2(ALU_A_Register__2_2), ._1_2(ALU_A_Register__1_2), ._0_2(ALU_A_Register__0_2),
    ._8_Bit_Output(ALU_A_Register__8_bit_output));
  DotMatrix #(.matrixcols(8), .matrixrows(1)) dotmatrix_3 (
    .col0(ALU_A_Register__7_2), .col1(ALU_A_Register__6_2), .col2(ALU_A_Register__5_2),
    .col3(ALU_A_Register__4_2), .col4(ALU_A_Register__3_2), .col5(ALU_A_Register__2_2),
    .col6(ALU_A_Register__1_2), .col7(ALU_A_Register__0_2));
  ALU ALU (
    ._7(program_2_add_loop_1__7), ._6(program_2_add_loop_1_out_9), ._5(program_2_add_loop_1_out_8),
    ._4(program_2_add_loop_1_out_7), ._3(program_2_add_loop_1_out_6), ._2(program_2_add_loop_1_out_5),
    ._1(program_2_add_loop_1_out_4), ._0(program_2_add_loop_1__0),
    .Enable(program_2_add_loop_1__3___alu_enable), .Subtract(program_2_add_loop_1__4___alu_subtract),
    .A7(ALU_A_Register__8_bit_output[7]), .A6(ALU_A_Register__8_bit_output[6]),
    .A5(ALU_A_Register__8_bit_output[5]), .A4(ALU_A_Register__8_bit_output[4]),
    .A3(ALU_A_Register__8_bit_output[3]), .A2(ALU_A_Register__8_bit_output[2]),
    .A1(ALU_A_Register__8_bit_output[1]), .A0(ALU_A_Register__8_bit_output[0]),
    .B7(ALU_B_Register__8_bit_output[7]), .B6(ALU_B_Register__8_bit_output[6]),
    .B5(ALU_B_Register__8_bit_output[5]), .B4(ALU_B_Register__8_bit_output[4]),
    .B3(ALU_B_Register__8_bit_output[3]), .B2(ALU_B_Register__8_bit_output[2]),
    .B1(ALU_B_Register__8_bit_output[1]), .B0(ALU_B_Register__8_bit_output[0]));

  // Notes on the sheet:
  //   Write
  //   Read
  //   ALU
  //   RAM
endmodule

module Clock (
  input  Clock,
  input  Clock_Select,
  input  Step_Select,
  input  Halt,
  input  Step,
  output Clock_Status,
  output Value
);

  wire and_1_out, and_2_out, not_2_out, or_1_out, Switch_q;

  Switch Switch (.in_1(Clock_Select), .in_2(or_1_out), .Q(Switch_q));
  or or_1 (or_1_out, Step_Select, Halt);
  not not_1 (Clock_Status, Switch_q);
  and and_1 (and_1_out, Clock, Clock_Status);
  and and_2 (and_2_out, Step, not_2_out);
  not not_2 (not_2_out, Clock_Status);
  or or_2 (Value, and_1_out, and_2_out);

  // Notes on the sheet:
  //   1 = ON, 0 = OFF
  //   When Step is triggered, it will
  //   advance the clock 1 tick
endmodule

module SR_Latch (
  input  in_1,
  input  in_2,
  output Q,
  output nQ
);

  nor nor_1 (Q, in_1, nQ);
  nor nor_2 (nQ, Q, in_2);
endmodule

module Switch (
  input  in_1,
  input  in_2,
  output Q
);

  SR_Latch SR_Latch (.in_1(in_1), .in_2(in_2), .Q(Q));  // open: nQ
endmodule

module _8_Bit_Register (
  input  CLK,
  input  Load,
  input  _7,
  input  _6,
  input  _5,
  input  _4,
  input  _3,
  input  _2,
  input  _1,
  input  _0,
  output _7_2,
  output _6_2,
  output _5_2,
  output _4_2,
  output _3_2,
  output _2_2,
  output _1_2,
  output _0_2,
  output [7:0] _8_Bit_Output
);

  _1_Bit_Register Bit_0 (.CLK(CLK), .Load(Load), .Data(_0), .Output(_0_2));
  _1_Bit_Register Bit_1 (.CLK(CLK), .Load(Load), .Data(_1), .Output(_1_2));
  _1_Bit_Register Bit_2 (.CLK(CLK), .Load(Load), .Data(_2), .Output(_2_2));
  _1_Bit_Register Bit_3 (.CLK(CLK), .Load(Load), .Data(_3), .Output(_3_2));
  _1_Bit_Register Bit_4 (.CLK(CLK), .Load(Load), .Data(_4), .Output(_4_2));
  _1_Bit_Register Bit_5 (.CLK(CLK), .Load(Load), .Data(_5), .Output(_5_2));
  _1_Bit_Register Bit_6 (.CLK(CLK), .Load(Load), .Data(_6), .Output(_6_2));
  _1_Bit_Register Bit_7 (.CLK(CLK), .Load(Load), .Data(_7), .Output(_7_2));

  assign _8_Bit_Output = {_7_2, _6_2, _5_2, _4_2, _3_2, _2_2, _1_2, _0_2};
endmodule

module _1_Bit_Register (
  input  CLK,
  input  Load,
  input  Data,
  output Output
);

  wire and_1_out, and_2_out, controlled_buffer_1_out, not_1_out, or_1_out;

  assign controlled_buffer_1_out = Load ? Data : 1'bz;  // Controlled_Buffer controlled_buffer_1
  not not_1 (not_1_out, Load);
  and and_1 (and_1_out, Load, controlled_buffer_1_out);
  or or_1 (or_1_out, and_1_out, and_2_out);
  and and_2 (and_2_out, not_1_out, Output);
  D_Flip_Flop d_ff_1 (.clk(CLK), .D(or_1_out), .Q(Output));  // open: Qn, preset, en, reset
endmodule

module ALU (
  input  A7,
  input  A6,
  input  A5,
  input  A4,
  input  A3,
  input  A2,
  input  A1,
  input  A0,
  input  Enable,
  input  Subtract,
  input  B7,
  input  B6,
  input  B5,
  input  B4,
  input  B3,
  input  B2,
  input  B1,
  input  B0,
  output _7,
  output _6,
  output _5,
  output _4,
  output _3,
  output _2,
  output _1,
  output _0
);

  wire adder_1__0, adder_1__1, adder_1__2, adder_1__3, adder_1__4, adder_1__5, adder_1__6, adder_1__7,
       xor_1_out, xor_2_out, xor_3_out, xor_4_out, xor_5_out, xor_6_out, xor_7_out, xor_8_out;

  assign _7 = Enable ? adder_1__7 : 1'bz;  // Controlled_Buffer controlled_buffer_1
  assign _6 = Enable ? adder_1__6 : 1'bz;  // Controlled_Buffer controlled_buffer_2
  assign _5 = Enable ? adder_1__5 : 1'bz;  // Controlled_Buffer controlled_buffer_3
  assign _4 = Enable ? adder_1__4 : 1'bz;  // Controlled_Buffer controlled_buffer_4
  assign _3 = Enable ? adder_1__3 : 1'bz;  // Controlled_Buffer controlled_buffer_5
  assign _2 = Enable ? adder_1__2 : 1'bz;  // Controlled_Buffer controlled_buffer_6
  assign _1 = Enable ? adder_1__1 : 1'bz;  // Controlled_Buffer controlled_buffer_7
  assign _0 = Enable ? adder_1__0 : 1'bz;  // Controlled_Buffer controlled_buffer_8
  xor xor_1 (xor_1_out, B7, Subtract);
  Adder adder_1 (
    ._7(adder_1__7), ._6(adder_1__6), ._5(adder_1__5), ._4(adder_1__4), ._3(adder_1__3), ._2(adder_1__2),
    ._1(adder_1__1), ._0(adder_1__0), .A7(A7), .A6(A6), .A5(A5), .A4(A4), .A3(A3), .A2(A2), .A1(A1), .A0(A0),
    .B7(xor_1_out), .B6(xor_2_out), .B5(xor_3_out), .B4(xor_4_out), .B3(xor_5_out), .B2(xor_6_out),
    .B1(xor_7_out), .B0(xor_8_out), .Carry_In(Subtract));
  xor xor_2 (xor_2_out, B6, Subtract);
  xor xor_3 (xor_3_out, B5, Subtract);
  xor xor_4 (xor_4_out, B4, Subtract);
  xor xor_5 (xor_5_out, B3, Subtract);
  xor xor_6 (xor_6_out, B2, Subtract);
  xor xor_7 (xor_7_out, B1, Subtract);
  xor xor_8 (xor_8_out, B0, Subtract);
endmodule

module Adder (
  input  A7,
  input  A6,
  input  A5,
  input  A4,
  input  A3,
  input  A2,
  input  A1,
  input  A0,
  input  Carry_In,
  input  B7,
  input  B6,
  input  B5,
  input  B4,
  input  B3,
  input  B2,
  input  B1,
  input  B0,
  output _7,
  output _6,
  output _5,
  output _4,
  output _3,
  output _2,
  output _1,
  output _0
);

  wire n1_bit_adder_2_carry_out, n1_bit_adder_3_carry_out, n1_bit_adder_4_carry_out,
       n1_bit_adder_5_carry_out, n1_bit_adder_6_carry_out, n1_bit_adder_7_carry_out, n1_bit_adder_8_carry_out;

  _1_Bit_Adder u_1_bit_adder_1 (.Sum(_7), .A(A7), .B(B7), .Carry_In(n1_bit_adder_2_carry_out));  // open: Carry_Out
  _1_Bit_Adder u_1_bit_adder_2 (
    .Carry_Out(n1_bit_adder_2_carry_out), .Sum(_6), .A(A6), .B(B6), .Carry_In(n1_bit_adder_3_carry_out));
  _1_Bit_Adder u_1_bit_adder_3 (
    .Carry_Out(n1_bit_adder_3_carry_out), .Sum(_5), .A(A5), .B(B5), .Carry_In(n1_bit_adder_4_carry_out));
  _1_Bit_Adder u_1_bit_adder_4 (
    .Carry_Out(n1_bit_adder_4_carry_out), .Sum(_4), .A(A4), .B(B4), .Carry_In(n1_bit_adder_5_carry_out));
  _1_Bit_Adder u_1_bit_adder_5 (
    .Carry_Out(n1_bit_adder_5_carry_out), .Sum(_3), .A(A3), .B(B3), .Carry_In(n1_bit_adder_7_carry_out));
  _1_Bit_Adder u_1_bit_adder_6 (
    .Carry_Out(n1_bit_adder_6_carry_out), .Sum(_1), .A(A1), .B(B1), .Carry_In(n1_bit_adder_8_carry_out));
  _1_Bit_Adder u_1_bit_adder_7 (
    .Carry_Out(n1_bit_adder_7_carry_out), .Sum(_2), .A(A2), .B(B2), .Carry_In(n1_bit_adder_6_carry_out));
  _1_Bit_Adder u_1_bit_adder_8 (.Carry_Out(n1_bit_adder_8_carry_out), .Sum(_0), .A(A0), .B(B0), .Carry_In(Carry_In));
endmodule

module _1_Bit_Adder (
  input  Carry_In,
  input  A,
  input  B,
  output Carry_Out,
  output Sum
);

  wire and_1_out, and_2_out, and_3_out, and_4_out, and_5_out, and_6_out, and_7_out, and_8_out, not_1_out,
       not_2_out, not_3_out, not_4_out, not_5_out, not_6_out, not_7_out, not_8_out, not_9_out;

  not not_1 (not_1_out, A);
  not not_2 (not_2_out, B);
  and and_1 (and_1_out, not_1_out, not_2_out, Carry_In);
  not not_3 (not_3_out, A);
  and and_2 (and_2_out, not_3_out, B, not_4_out);
  not not_4 (not_4_out, Carry_In);
  not not_5 (not_5_out, B);
  and and_3 (and_3_out, A, not_5_out, not_6_out);
  not not_6 (not_6_out, Carry_In);
  and and_4 (and_4_out, A, B, Carry_In);
  not not_7 (not_7_out, A);
  and and_5 (and_5_out, not_7_out, B, Carry_In);
  not not_8 (not_8_out, B);
  and and_6 (and_6_out, A, not_8_out, Carry_In);
  and and_7 (and_7_out, A, B, not_9_out);
  not not_9 (not_9_out, Carry_In);
  and and_8 (and_8_out, A, B, Carry_In);
  or or_1 (Sum, and_1_out, and_2_out, and_3_out, and_4_out);
  or or_2 (Carry_Out, and_5_out, and_6_out, and_7_out, and_8_out);
  // OR_Gate or_3 is placed but not wired
endmodule

module _8_Bit_RAM (
  input  A7,
  input  A6,
  input  A5,
  input  A4,
  input  A3,
  input  A2,
  input  A1,
  input  A0,
  input  CLK,
  input  Load,
  input  Unload,
  output out_12,
  output out_13,
  output out_14,
  output out_15,
  output out_16,
  output out_17,
  output out_18,
  output out_19,
  output [7:0] out_20
);

  _1_Bit_Register u_1_bit_register_1 (.CLK(CLK), .Load(Load), .Data(A7), .Output(out_12));
  _1_Bit_Register u_1_bit_register_2 (.CLK(CLK), .Load(Load), .Data(A6), .Output(out_13));
  _1_Bit_Register u_1_bit_register_3 (.CLK(CLK), .Load(Load), .Data(A5), .Output(out_14));
  _1_Bit_Register u_1_bit_register_4 (.CLK(CLK), .Load(Load), .Data(A4), .Output(out_15));
  _1_Bit_Register u_1_bit_register_5 (.CLK(CLK), .Load(Load), .Data(A3), .Output(out_16));
  _1_Bit_Register u_1_bit_register_6 (.CLK(CLK), .Load(Load), .Data(A2), .Output(out_17));
  _1_Bit_Register u_1_bit_register_7 (.CLK(CLK), .Load(Load), .Data(A1), .Output(out_18));
  _1_Bit_Register u_1_bit_register_8 (.CLK(CLK), .Load(Load), .Data(A0), .Output(out_19));
  assign out_20 = Unload ? {out_12, out_13, out_14, out_15, out_16, out_17, out_18, out_19} : 8'bz;  // Controlled_Buffer controlled_buffer_1
endmodule

module RAM (
  input  CLK,
  input  in_2,
  input  in_3,
  input  in_4,
  input  in_5,
  input  in_6,
  input  in_7,
  input  in_8,
  input  in_9,
  input  in_10,
  input  [3:0] Write_Address,
  input  [3:0] Read_Address,
  input  Read,
  output out_14,
  output out_15,
  output out_16,
  output out_17,
  output out_18,
  output out_19,
  output out_20,
  output out_21
);

  wire decoder_1_out1, decoder_1_out2, decoder_1_out3, decoder_1_out4, decoder_1_out5, decoder_1_out6,
       decoder_1_out7, decoder_1_out8, decoder_1_out9, decoder_1_out10, decoder_1_out11, decoder_1_out12,
       decoder_1_out13, decoder_1_out14, decoder_1_out15, decoder_2_out1, decoder_2_out2, decoder_2_out3,
       decoder_2_out4, decoder_2_out5, decoder_2_out6, decoder_2_out7, decoder_2_out8, decoder_2_out9,
       decoder_2_out10, decoder_2_out11, decoder_2_out12, decoder_2_out13, decoder_2_out14, decoder_2_out15,
       n8_bit_ram_1_out_12, n8_bit_ram_1_out_13, n8_bit_ram_1_out_14, n8_bit_ram_1_out_15,
       n8_bit_ram_1_out_16, n8_bit_ram_1_out_17, n8_bit_ram_1_out_18, n8_bit_ram_1_out_19,
       n8_bit_ram_2_out_12, n8_bit_ram_2_out_13, n8_bit_ram_2_out_14, n8_bit_ram_2_out_15,
       n8_bit_ram_2_out_16, n8_bit_ram_2_out_17, n8_bit_ram_2_out_18, n8_bit_ram_2_out_19,
       n8_bit_ram_3_out_12, n8_bit_ram_3_out_13, n8_bit_ram_3_out_14, n8_bit_ram_3_out_15,
       n8_bit_ram_3_out_16, n8_bit_ram_3_out_17, n8_bit_ram_3_out_18, n8_bit_ram_3_out_19,
       n8_bit_ram_4_out_12, n8_bit_ram_4_out_13, n8_bit_ram_4_out_14, n8_bit_ram_4_out_15,
       n8_bit_ram_4_out_16, n8_bit_ram_4_out_17, n8_bit_ram_4_out_18, n8_bit_ram_4_out_19,
       n8_bit_ram_5_out_12, n8_bit_ram_5_out_13, n8_bit_ram_5_out_14, n8_bit_ram_5_out_15,
       n8_bit_ram_5_out_16, n8_bit_ram_5_out_17, n8_bit_ram_5_out_18, n8_bit_ram_5_out_19,
       n8_bit_ram_6_out_12, n8_bit_ram_6_out_13, n8_bit_ram_6_out_14, n8_bit_ram_6_out_15,
       n8_bit_ram_6_out_16, n8_bit_ram_6_out_17, n8_bit_ram_6_out_18, n8_bit_ram_6_out_19,
       n8_bit_ram_7_out_12, n8_bit_ram_7_out_13, n8_bit_ram_7_out_14, n8_bit_ram_7_out_15,
       n8_bit_ram_7_out_16, n8_bit_ram_7_out_17, n8_bit_ram_7_out_18, n8_bit_ram_7_out_19,
       n8_bit_ram_8_out_12, n8_bit_ram_8_out_13, n8_bit_ram_8_out_14, n8_bit_ram_8_out_15,
       n8_bit_ram_8_out_16, n8_bit_ram_8_out_17, n8_bit_ram_8_out_18, n8_bit_ram_8_out_19,
       n8_bit_ram_9_out_12, n8_bit_ram_9_out_13, n8_bit_ram_9_out_14, n8_bit_ram_9_out_15,
       n8_bit_ram_9_out_16, n8_bit_ram_9_out_17, n8_bit_ram_9_out_18, n8_bit_ram_9_out_19,
       n8_bit_ram_10_out_12, n8_bit_ram_10_out_13, n8_bit_ram_10_out_14, n8_bit_ram_10_out_15,
       n8_bit_ram_10_out_16, n8_bit_ram_10_out_17, n8_bit_ram_10_out_18, n8_bit_ram_10_out_19,
       n8_bit_ram_11_out_12, n8_bit_ram_11_out_13, n8_bit_ram_11_out_14, n8_bit_ram_11_out_15,
       n8_bit_ram_11_out_16, n8_bit_ram_11_out_17, n8_bit_ram_11_out_18, n8_bit_ram_11_out_19,
       n8_bit_ram_12_out_12, n8_bit_ram_12_out_13, n8_bit_ram_12_out_14, n8_bit_ram_12_out_15,
       n8_bit_ram_12_out_16, n8_bit_ram_12_out_17, n8_bit_ram_12_out_18, n8_bit_ram_12_out_19,
       n8_bit_ram_13_out_12, n8_bit_ram_13_out_13, n8_bit_ram_13_out_14, n8_bit_ram_13_out_15,
       n8_bit_ram_13_out_16, n8_bit_ram_13_out_17, n8_bit_ram_13_out_18, n8_bit_ram_13_out_19,
       n8_bit_ram_14_out_12, n8_bit_ram_14_out_13, n8_bit_ram_14_out_14, n8_bit_ram_14_out_15,
       n8_bit_ram_14_out_16, n8_bit_ram_14_out_17, n8_bit_ram_14_out_18, n8_bit_ram_14_out_19,
       n8_bit_ram_15_out_12, n8_bit_ram_15_out_13, n8_bit_ram_15_out_14, n8_bit_ram_15_out_15,
       n8_bit_ram_15_out_16, n8_bit_ram_15_out_17, n8_bit_ram_15_out_18, n8_bit_ram_15_out_19;
  wire [7:0] n8_bit_ram_1_out_20;

  Decoder #(.select(4)) decoder_1 (
    .out1(decoder_1_out1), .out2(decoder_1_out2), .out3(decoder_1_out3), .out4(decoder_1_out4),
    .out5(decoder_1_out5), .out6(decoder_1_out6), .out7(decoder_1_out7), .out8(decoder_1_out8),
    .out9(decoder_1_out9), .out10(decoder_1_out10), .out11(decoder_1_out11), .out12(decoder_1_out12),
    .out13(decoder_1_out13), .out14(decoder_1_out14), .out15(decoder_1_out15), .sel(Read_Address));  // open: out0, en
  Decoder #(.select(4)) decoder_2 (
    .out1(decoder_2_out1), .out2(decoder_2_out2), .out3(decoder_2_out3), .out4(decoder_2_out4),
    .out5(decoder_2_out5), .out6(decoder_2_out6), .out7(decoder_2_out7), .out8(decoder_2_out8),
    .out9(decoder_2_out9), .out10(decoder_2_out10), .out11(decoder_2_out11), .out12(decoder_2_out12),
    .out13(decoder_2_out13), .out14(decoder_2_out14), .out15(decoder_2_out15), .sel(Write_Address));  // open: out0, en
  assign out_14 = Read ? n8_bit_ram_1_out_20[7] : 1'bz;  // Controlled_Buffer controlled_buffer_1
  assign out_15 = Read ? n8_bit_ram_1_out_20[6] : 1'bz;  // Controlled_Buffer controlled_buffer_2
  assign n8_bit_ram_1_out_20[5] = in_10 ? in_4 : 1'bz;  // Controlled_Buffer controlled_buffer_3
  assign n8_bit_ram_1_out_20[7] = in_10 ? in_2 : 1'bz;  // Controlled_Buffer controlled_buffer_4
  assign n8_bit_ram_1_out_20[6] = in_10 ? in_3 : 1'bz;  // Controlled_Buffer controlled_buffer_5
  assign out_16 = Read ? n8_bit_ram_1_out_20[5] : 1'bz;  // Controlled_Buffer controlled_buffer_6
  assign out_17 = Read ? n8_bit_ram_1_out_20[4] : 1'bz;  // Controlled_Buffer controlled_buffer_7
  assign out_18 = Read ? n8_bit_ram_1_out_20[3] : 1'bz;  // Controlled_Buffer controlled_buffer_8
  assign n8_bit_ram_1_out_20[2] = in_10 ? in_7 : 1'bz;  // Controlled_Buffer controlled_buffer_9
  assign n8_bit_ram_1_out_20[3] = in_10 ? in_6 : 1'bz;  // Controlled_Buffer controlled_buffer_10
  assign n8_bit_ram_1_out_20[1] = in_10 ? in_8 : 1'bz;  // Controlled_Buffer controlled_buffer_11
  assign n8_bit_ram_1_out_20[4] = in_10 ? in_5 : 1'bz;  // Controlled_Buffer controlled_buffer_12
  DotMatrix #(.matrixcols(8), .matrixrows(1)) dotmatrix_1 (
    .col0(n8_bit_ram_1_out_20[7]), .col1(n8_bit_ram_1_out_20[6]), .col2(n8_bit_ram_1_out_20[5]),
    .col3(n8_bit_ram_1_out_20[4]), .col4(n8_bit_ram_1_out_20[3]), .col5(n8_bit_ram_1_out_20[2]),
    .col6(n8_bit_ram_1_out_20[1]), .col7(n8_bit_ram_1_out_20[0]));
  _8_Bit_RAM u_8_bit_ram_1 (
    .CLK(CLK), .Load(decoder_2_out1), .Unload(decoder_1_out1), .A7(n8_bit_ram_1_out_20[7]),
    .A6(n8_bit_ram_1_out_20[6]), .A5(n8_bit_ram_1_out_20[5]), .A4(n8_bit_ram_1_out_20[4]),
    .A3(n8_bit_ram_1_out_20[3]), .A2(n8_bit_ram_1_out_20[2]), .A1(n8_bit_ram_1_out_20[1]),
    .A0(n8_bit_ram_1_out_20[0]), .out_12(n8_bit_ram_1_out_12), .out_13(n8_bit_ram_1_out_13),
    .out_14(n8_bit_ram_1_out_14), .out_15(n8_bit_ram_1_out_15), .out_16(n8_bit_ram_1_out_16),
    .out_17(n8_bit_ram_1_out_17), .out_18(n8_bit_ram_1_out_18), .out_19(n8_bit_ram_1_out_19),
    .out_20(n8_bit_ram_1_out_20));
  DotMatrix #(.matrixcols(8), .matrixrows(1)) dotmatrix_2 (
    .col0(n8_bit_ram_1_out_12), .col1(n8_bit_ram_1_out_13), .col2(n8_bit_ram_1_out_14),
    .col3(n8_bit_ram_1_out_15), .col4(n8_bit_ram_1_out_16), .col5(n8_bit_ram_1_out_17),
    .col6(n8_bit_ram_1_out_18), .col7(n8_bit_ram_1_out_19));
  _8_Bit_RAM u_8_bit_ram_2 (
    .CLK(CLK), .Load(decoder_2_out2), .Unload(decoder_1_out2), .A7(n8_bit_ram_1_out_20[7]),
    .A6(n8_bit_ram_1_out_20[6]), .A5(n8_bit_ram_1_out_20[5]), .A4(n8_bit_ram_1_out_20[4]),
    .A3(n8_bit_ram_1_out_20[3]), .A2(n8_bit_ram_1_out_20[2]), .A1(n8_bit_ram_1_out_20[1]),
    .A0(n8_bit_ram_1_out_20[0]), .out_12(n8_bit_ram_2_out_12), .out_13(n8_bit_ram_2_out_13),
    .out_14(n8_bit_ram_2_out_14), .out_15(n8_bit_ram_2_out_15), .out_16(n8_bit_ram_2_out_16),
    .out_17(n8_bit_ram_2_out_17), .out_18(n8_bit_ram_2_out_18), .out_19(n8_bit_ram_2_out_19),
    .out_20(n8_bit_ram_1_out_20));
  DotMatrix #(.matrixcols(8), .matrixrows(1)) dotmatrix_3 (
    .col0(n8_bit_ram_2_out_12), .col1(n8_bit_ram_2_out_13), .col2(n8_bit_ram_2_out_14),
    .col3(n8_bit_ram_2_out_15), .col4(n8_bit_ram_2_out_16), .col5(n8_bit_ram_2_out_17),
    .col6(n8_bit_ram_2_out_18), .col7(n8_bit_ram_2_out_19));
  _8_Bit_RAM u_8_bit_ram_3 (
    .CLK(CLK), .Load(decoder_2_out3), .Unload(decoder_1_out3), .A7(n8_bit_ram_1_out_20[7]),
    .A6(n8_bit_ram_1_out_20[6]), .A5(n8_bit_ram_1_out_20[5]), .A4(n8_bit_ram_1_out_20[4]),
    .A3(n8_bit_ram_1_out_20[3]), .A2(n8_bit_ram_1_out_20[2]), .A1(n8_bit_ram_1_out_20[1]),
    .A0(n8_bit_ram_1_out_20[0]), .out_12(n8_bit_ram_3_out_12), .out_13(n8_bit_ram_3_out_13),
    .out_14(n8_bit_ram_3_out_14), .out_15(n8_bit_ram_3_out_15), .out_16(n8_bit_ram_3_out_16),
    .out_17(n8_bit_ram_3_out_17), .out_18(n8_bit_ram_3_out_18), .out_19(n8_bit_ram_3_out_19),
    .out_20(n8_bit_ram_1_out_20));
  DotMatrix #(.matrixcols(8), .matrixrows(1)) dotmatrix_4 (
    .col0(n8_bit_ram_3_out_12), .col1(n8_bit_ram_3_out_13), .col2(n8_bit_ram_3_out_14),
    .col3(n8_bit_ram_3_out_15), .col4(n8_bit_ram_3_out_16), .col5(n8_bit_ram_3_out_17),
    .col6(n8_bit_ram_3_out_18), .col7(n8_bit_ram_3_out_19));
  _8_Bit_RAM u_8_bit_ram_4 (
    .CLK(CLK), .Load(decoder_2_out4), .Unload(decoder_1_out4), .A7(n8_bit_ram_1_out_20[7]),
    .A6(n8_bit_ram_1_out_20[6]), .A5(n8_bit_ram_1_out_20[5]), .A4(n8_bit_ram_1_out_20[4]),
    .A3(n8_bit_ram_1_out_20[3]), .A2(n8_bit_ram_1_out_20[2]), .A1(n8_bit_ram_1_out_20[1]),
    .A0(n8_bit_ram_1_out_20[0]), .out_12(n8_bit_ram_4_out_12), .out_13(n8_bit_ram_4_out_13),
    .out_14(n8_bit_ram_4_out_14), .out_15(n8_bit_ram_4_out_15), .out_16(n8_bit_ram_4_out_16),
    .out_17(n8_bit_ram_4_out_17), .out_18(n8_bit_ram_4_out_18), .out_19(n8_bit_ram_4_out_19),
    .out_20(n8_bit_ram_1_out_20));
  DotMatrix #(.matrixcols(8), .matrixrows(1)) dotmatrix_5 (
    .col0(n8_bit_ram_4_out_12), .col1(n8_bit_ram_4_out_13), .col2(n8_bit_ram_4_out_14),
    .col3(n8_bit_ram_4_out_15), .col4(n8_bit_ram_4_out_16), .col5(n8_bit_ram_4_out_17),
    .col6(n8_bit_ram_4_out_18), .col7(n8_bit_ram_4_out_19));
  _8_Bit_RAM u_8_bit_ram_5 (
    .CLK(CLK), .Load(decoder_2_out5), .Unload(decoder_1_out5), .A7(n8_bit_ram_1_out_20[7]),
    .A6(n8_bit_ram_1_out_20[6]), .A5(n8_bit_ram_1_out_20[5]), .A4(n8_bit_ram_1_out_20[4]),
    .A3(n8_bit_ram_1_out_20[3]), .A2(n8_bit_ram_1_out_20[2]), .A1(n8_bit_ram_1_out_20[1]),
    .A0(n8_bit_ram_1_out_20[0]), .out_12(n8_bit_ram_5_out_12), .out_13(n8_bit_ram_5_out_13),
    .out_14(n8_bit_ram_5_out_14), .out_15(n8_bit_ram_5_out_15), .out_16(n8_bit_ram_5_out_16),
    .out_17(n8_bit_ram_5_out_17), .out_18(n8_bit_ram_5_out_18), .out_19(n8_bit_ram_5_out_19),
    .out_20(n8_bit_ram_1_out_20));
  DotMatrix #(.matrixcols(8), .matrixrows(1)) dotmatrix_6 (
    .col0(n8_bit_ram_5_out_12), .col1(n8_bit_ram_5_out_13), .col2(n8_bit_ram_5_out_14),
    .col3(n8_bit_ram_5_out_15), .col4(n8_bit_ram_5_out_16), .col5(n8_bit_ram_5_out_17),
    .col6(n8_bit_ram_5_out_18), .col7(n8_bit_ram_5_out_19));
  _8_Bit_RAM u_8_bit_ram_6 (
    .CLK(CLK), .Load(decoder_2_out6), .Unload(decoder_1_out6), .A7(n8_bit_ram_1_out_20[7]),
    .A6(n8_bit_ram_1_out_20[6]), .A5(n8_bit_ram_1_out_20[5]), .A4(n8_bit_ram_1_out_20[4]),
    .A3(n8_bit_ram_1_out_20[3]), .A2(n8_bit_ram_1_out_20[2]), .A1(n8_bit_ram_1_out_20[1]),
    .A0(n8_bit_ram_1_out_20[0]), .out_12(n8_bit_ram_6_out_12), .out_13(n8_bit_ram_6_out_13),
    .out_14(n8_bit_ram_6_out_14), .out_15(n8_bit_ram_6_out_15), .out_16(n8_bit_ram_6_out_16),
    .out_17(n8_bit_ram_6_out_17), .out_18(n8_bit_ram_6_out_18), .out_19(n8_bit_ram_6_out_19),
    .out_20(n8_bit_ram_1_out_20));
  DotMatrix #(.matrixcols(8), .matrixrows(1)) dotmatrix_7 (
    .col0(n8_bit_ram_6_out_12), .col1(n8_bit_ram_6_out_13), .col2(n8_bit_ram_6_out_14),
    .col3(n8_bit_ram_6_out_15), .col4(n8_bit_ram_6_out_16), .col5(n8_bit_ram_6_out_17),
    .col6(n8_bit_ram_6_out_18), .col7(n8_bit_ram_6_out_19));
  _8_Bit_RAM u_8_bit_ram_7 (
    .CLK(CLK), .Load(decoder_2_out7), .Unload(decoder_1_out7), .A7(n8_bit_ram_1_out_20[7]),
    .A6(n8_bit_ram_1_out_20[6]), .A5(n8_bit_ram_1_out_20[5]), .A4(n8_bit_ram_1_out_20[4]),
    .A3(n8_bit_ram_1_out_20[3]), .A2(n8_bit_ram_1_out_20[2]), .A1(n8_bit_ram_1_out_20[1]),
    .A0(n8_bit_ram_1_out_20[0]), .out_12(n8_bit_ram_7_out_12), .out_13(n8_bit_ram_7_out_13),
    .out_14(n8_bit_ram_7_out_14), .out_15(n8_bit_ram_7_out_15), .out_16(n8_bit_ram_7_out_16),
    .out_17(n8_bit_ram_7_out_17), .out_18(n8_bit_ram_7_out_18), .out_19(n8_bit_ram_7_out_19),
    .out_20(n8_bit_ram_1_out_20));
  DotMatrix #(.matrixcols(8), .matrixrows(1)) dotmatrix_8 (
    .col0(n8_bit_ram_7_out_12), .col1(n8_bit_ram_7_out_13), .col2(n8_bit_ram_7_out_14),
    .col3(n8_bit_ram_7_out_15), .col4(n8_bit_ram_7_out_16), .col5(n8_bit_ram_7_out_17),
    .col6(n8_bit_ram_7_out_18), .col7(n8_bit_ram_7_out_19));
  _8_Bit_RAM u_8_bit_ram_8 (
    .CLK(CLK), .Load(decoder_2_out8), .Unload(decoder_1_out8), .A7(n8_bit_ram_1_out_20[7]),
    .A6(n8_bit_ram_1_out_20[6]), .A5(n8_bit_ram_1_out_20[5]), .A4(n8_bit_ram_1_out_20[4]),
    .A3(n8_bit_ram_1_out_20[3]), .A2(n8_bit_ram_1_out_20[2]), .A1(n8_bit_ram_1_out_20[1]),
    .A0(n8_bit_ram_1_out_20[0]), .out_12(n8_bit_ram_8_out_12), .out_13(n8_bit_ram_8_out_13),
    .out_14(n8_bit_ram_8_out_14), .out_15(n8_bit_ram_8_out_15), .out_16(n8_bit_ram_8_out_16),
    .out_17(n8_bit_ram_8_out_17), .out_18(n8_bit_ram_8_out_18), .out_19(n8_bit_ram_8_out_19),
    .out_20(n8_bit_ram_1_out_20));
  DotMatrix #(.matrixcols(8), .matrixrows(1)) dotmatrix_9 (
    .col0(n8_bit_ram_8_out_12), .col1(n8_bit_ram_8_out_13), .col2(n8_bit_ram_8_out_14),
    .col3(n8_bit_ram_8_out_15), .col4(n8_bit_ram_8_out_16), .col5(n8_bit_ram_8_out_17),
    .col6(n8_bit_ram_8_out_18), .col7(n8_bit_ram_8_out_19));
  _8_Bit_RAM u_8_bit_ram_9 (
    .CLK(CLK), .Load(decoder_2_out9), .Unload(decoder_1_out9), .A7(n8_bit_ram_1_out_20[7]),
    .A6(n8_bit_ram_1_out_20[6]), .A5(n8_bit_ram_1_out_20[5]), .A4(n8_bit_ram_1_out_20[4]),
    .A3(n8_bit_ram_1_out_20[3]), .A2(n8_bit_ram_1_out_20[2]), .A1(n8_bit_ram_1_out_20[1]),
    .A0(n8_bit_ram_1_out_20[0]), .out_12(n8_bit_ram_9_out_12), .out_13(n8_bit_ram_9_out_13),
    .out_14(n8_bit_ram_9_out_14), .out_15(n8_bit_ram_9_out_15), .out_16(n8_bit_ram_9_out_16),
    .out_17(n8_bit_ram_9_out_17), .out_18(n8_bit_ram_9_out_18), .out_19(n8_bit_ram_9_out_19),
    .out_20(n8_bit_ram_1_out_20));
  DotMatrix #(.matrixcols(8), .matrixrows(1)) dotmatrix_10 (
    .col0(n8_bit_ram_9_out_12), .col1(n8_bit_ram_9_out_13), .col2(n8_bit_ram_9_out_14),
    .col3(n8_bit_ram_9_out_15), .col4(n8_bit_ram_9_out_16), .col5(n8_bit_ram_9_out_17),
    .col6(n8_bit_ram_9_out_18), .col7(n8_bit_ram_9_out_19));
  _8_Bit_RAM u_8_bit_ram_10 (
    .CLK(CLK), .Load(decoder_2_out10), .Unload(decoder_1_out10), .A7(n8_bit_ram_1_out_20[7]),
    .A6(n8_bit_ram_1_out_20[6]), .A5(n8_bit_ram_1_out_20[5]), .A4(n8_bit_ram_1_out_20[4]),
    .A3(n8_bit_ram_1_out_20[3]), .A2(n8_bit_ram_1_out_20[2]), .A1(n8_bit_ram_1_out_20[1]),
    .A0(n8_bit_ram_1_out_20[0]), .out_12(n8_bit_ram_10_out_12), .out_13(n8_bit_ram_10_out_13),
    .out_14(n8_bit_ram_10_out_14), .out_15(n8_bit_ram_10_out_15), .out_16(n8_bit_ram_10_out_16),
    .out_17(n8_bit_ram_10_out_17), .out_18(n8_bit_ram_10_out_18), .out_19(n8_bit_ram_10_out_19),
    .out_20(n8_bit_ram_1_out_20));
  DotMatrix #(.matrixcols(8), .matrixrows(1)) dotmatrix_11 (
    .col0(n8_bit_ram_10_out_12), .col1(n8_bit_ram_10_out_13), .col2(n8_bit_ram_10_out_14),
    .col3(n8_bit_ram_10_out_15), .col4(n8_bit_ram_10_out_16), .col5(n8_bit_ram_10_out_17),
    .col6(n8_bit_ram_10_out_18), .col7(n8_bit_ram_10_out_19));
  _8_Bit_RAM u_8_bit_ram_11 (
    .CLK(CLK), .Load(decoder_2_out11), .Unload(decoder_1_out11), .A7(n8_bit_ram_1_out_20[7]),
    .A6(n8_bit_ram_1_out_20[6]), .A5(n8_bit_ram_1_out_20[5]), .A4(n8_bit_ram_1_out_20[4]),
    .A3(n8_bit_ram_1_out_20[3]), .A2(n8_bit_ram_1_out_20[2]), .A1(n8_bit_ram_1_out_20[1]),
    .A0(n8_bit_ram_1_out_20[0]), .out_12(n8_bit_ram_11_out_12), .out_13(n8_bit_ram_11_out_13),
    .out_14(n8_bit_ram_11_out_14), .out_15(n8_bit_ram_11_out_15), .out_16(n8_bit_ram_11_out_16),
    .out_17(n8_bit_ram_11_out_17), .out_18(n8_bit_ram_11_out_18), .out_19(n8_bit_ram_11_out_19),
    .out_20(n8_bit_ram_1_out_20));
  DotMatrix #(.matrixcols(8), .matrixrows(1)) dotmatrix_12 (
    .col0(n8_bit_ram_11_out_12), .col1(n8_bit_ram_11_out_13), .col2(n8_bit_ram_11_out_14),
    .col3(n8_bit_ram_11_out_15), .col4(n8_bit_ram_11_out_16), .col5(n8_bit_ram_11_out_17),
    .col6(n8_bit_ram_11_out_18), .col7(n8_bit_ram_11_out_19));
  _8_Bit_RAM u_8_bit_ram_12 (
    .CLK(CLK), .Load(decoder_2_out12), .Unload(decoder_1_out12), .A7(n8_bit_ram_1_out_20[7]),
    .A6(n8_bit_ram_1_out_20[6]), .A5(n8_bit_ram_1_out_20[5]), .A4(n8_bit_ram_1_out_20[4]),
    .A3(n8_bit_ram_1_out_20[3]), .A2(n8_bit_ram_1_out_20[2]), .A1(n8_bit_ram_1_out_20[1]),
    .A0(n8_bit_ram_1_out_20[0]), .out_12(n8_bit_ram_12_out_12), .out_13(n8_bit_ram_12_out_13),
    .out_14(n8_bit_ram_12_out_14), .out_15(n8_bit_ram_12_out_15), .out_16(n8_bit_ram_12_out_16),
    .out_17(n8_bit_ram_12_out_17), .out_18(n8_bit_ram_12_out_18), .out_19(n8_bit_ram_12_out_19),
    .out_20(n8_bit_ram_1_out_20));
  DotMatrix #(.matrixcols(8), .matrixrows(1)) dotmatrix_13 (
    .col0(n8_bit_ram_12_out_12), .col1(n8_bit_ram_12_out_13), .col2(n8_bit_ram_12_out_14),
    .col3(n8_bit_ram_12_out_15), .col4(n8_bit_ram_12_out_16), .col5(n8_bit_ram_12_out_17),
    .col6(n8_bit_ram_12_out_18), .col7(n8_bit_ram_12_out_19));
  _8_Bit_RAM u_8_bit_ram_13 (
    .CLK(CLK), .Load(decoder_2_out13), .Unload(decoder_1_out13), .A7(n8_bit_ram_1_out_20[7]),
    .A6(n8_bit_ram_1_out_20[6]), .A5(n8_bit_ram_1_out_20[5]), .A4(n8_bit_ram_1_out_20[4]),
    .A3(n8_bit_ram_1_out_20[3]), .A2(n8_bit_ram_1_out_20[2]), .A1(n8_bit_ram_1_out_20[1]),
    .A0(n8_bit_ram_1_out_20[0]), .out_12(n8_bit_ram_13_out_12), .out_13(n8_bit_ram_13_out_13),
    .out_14(n8_bit_ram_13_out_14), .out_15(n8_bit_ram_13_out_15), .out_16(n8_bit_ram_13_out_16),
    .out_17(n8_bit_ram_13_out_17), .out_18(n8_bit_ram_13_out_18), .out_19(n8_bit_ram_13_out_19),
    .out_20(n8_bit_ram_1_out_20));
  DotMatrix #(.matrixcols(8), .matrixrows(1)) dotmatrix_14 (
    .col0(n8_bit_ram_13_out_12), .col1(n8_bit_ram_13_out_13), .col2(n8_bit_ram_13_out_14),
    .col3(n8_bit_ram_13_out_15), .col4(n8_bit_ram_13_out_16), .col5(n8_bit_ram_13_out_17),
    .col6(n8_bit_ram_13_out_18), .col7(n8_bit_ram_13_out_19));
  _8_Bit_RAM u_8_bit_ram_14 (
    .CLK(CLK), .Load(decoder_2_out14), .Unload(decoder_1_out14), .A7(n8_bit_ram_1_out_20[7]),
    .A6(n8_bit_ram_1_out_20[6]), .A5(n8_bit_ram_1_out_20[5]), .A4(n8_bit_ram_1_out_20[4]),
    .A3(n8_bit_ram_1_out_20[3]), .A2(n8_bit_ram_1_out_20[2]), .A1(n8_bit_ram_1_out_20[1]),
    .A0(n8_bit_ram_1_out_20[0]), .out_12(n8_bit_ram_14_out_12), .out_13(n8_bit_ram_14_out_13),
    .out_14(n8_bit_ram_14_out_14), .out_15(n8_bit_ram_14_out_15), .out_16(n8_bit_ram_14_out_16),
    .out_17(n8_bit_ram_14_out_17), .out_18(n8_bit_ram_14_out_18), .out_19(n8_bit_ram_14_out_19),
    .out_20(n8_bit_ram_1_out_20));
  DotMatrix #(.matrixcols(8), .matrixrows(1)) dotmatrix_15 (
    .col0(n8_bit_ram_14_out_12), .col1(n8_bit_ram_14_out_13), .col2(n8_bit_ram_14_out_14),
    .col3(n8_bit_ram_14_out_15), .col4(n8_bit_ram_14_out_16), .col5(n8_bit_ram_14_out_17),
    .col6(n8_bit_ram_14_out_18), .col7(n8_bit_ram_14_out_19));
  _8_Bit_RAM u_8_bit_ram_15 (
    .CLK(CLK), .Load(decoder_2_out15), .Unload(decoder_1_out15), .A7(n8_bit_ram_1_out_20[7]),
    .A6(n8_bit_ram_1_out_20[6]), .A5(n8_bit_ram_1_out_20[5]), .A4(n8_bit_ram_1_out_20[4]),
    .A3(n8_bit_ram_1_out_20[3]), .A2(n8_bit_ram_1_out_20[2]), .A1(n8_bit_ram_1_out_20[1]),
    .A0(n8_bit_ram_1_out_20[0]), .out_12(n8_bit_ram_15_out_12), .out_13(n8_bit_ram_15_out_13),
    .out_14(n8_bit_ram_15_out_14), .out_15(n8_bit_ram_15_out_15), .out_16(n8_bit_ram_15_out_16),
    .out_17(n8_bit_ram_15_out_17), .out_18(n8_bit_ram_15_out_18), .out_19(n8_bit_ram_15_out_19),
    .out_20(n8_bit_ram_1_out_20));
  DotMatrix #(.matrixcols(8), .matrixrows(1)) dotmatrix_16 (
    .col0(n8_bit_ram_15_out_12), .col1(n8_bit_ram_15_out_13), .col2(n8_bit_ram_15_out_14),
    .col3(n8_bit_ram_15_out_15), .col4(n8_bit_ram_15_out_16), .col5(n8_bit_ram_15_out_17),
    .col6(n8_bit_ram_15_out_18), .col7(n8_bit_ram_15_out_19));
  assign out_20 = Read ? n8_bit_ram_1_out_20[1] : 1'bz;  // Controlled_Buffer controlled_buffer_13
  assign out_19 = Read ? n8_bit_ram_1_out_20[2] : 1'bz;  // Controlled_Buffer controlled_buffer_14
  assign n8_bit_ram_1_out_20[0] = in_10 ? in_9 : 1'bz;  // Controlled_Buffer controlled_buffer_15
  assign out_21 = Read ? n8_bit_ram_1_out_20[0] : 1'bz;  // Controlled_Buffer controlled_buffer_16
endmodule

module Program_Counter (
  input  [3:0] Jump_Address,
  input  CLK,
  input  Jump_Enable,
  input  Enable,
  output out_5,
  output out_6,
  output out_7,
  output out_8
);

  wire and_1_out, and_2_out, and_3_out, and_4_out, controlled_buffer_1_out, controlled_buffer_2_out,
       controlled_buffer_3_out, controlled_buffer_4_out, decoder_1_out0, decoder_1_out1, decoder_2_out0,
       decoder_2_out1, decoder_3_out0, decoder_3_out1, decoder_4_out0, decoder_4_out1;

  assign controlled_buffer_1_out = Jump_Enable ? Jump_Address[3] : 1'bz;  // Controlled_Buffer controlled_buffer_1
  Decoder decoder_1 (.out0(decoder_1_out0), .out1(decoder_1_out1), .sel(controlled_buffer_1_out));  // open: en
  and and_1 (and_1_out, Enable, out_6);
  assign controlled_buffer_2_out = Jump_Enable ? Jump_Address[2] : 1'bz;  // Controlled_Buffer controlled_buffer_2
  J_K_Flip_Flop #(.trigger("falling")) j_k_ff_1 (
    .J(1'b1), .clk(and_1_out), .K(1'b1), .Q(out_5), .preset(decoder_1_out1), .reset(decoder_1_out0));  // open: Qn, en
  Decoder decoder_2 (.out0(decoder_2_out0), .out1(decoder_2_out1), .sel(controlled_buffer_2_out));  // open: en
  J_K_Flip_Flop #(.trigger("falling")) j_k_ff_2 (
    .J(1'b1), .clk(and_2_out), .K(1'b1), .Q(out_6), .preset(decoder_2_out1), .reset(decoder_2_out0));  // open: Qn, en
  and and_2 (and_2_out, Enable, out_7);
  assign controlled_buffer_3_out = Jump_Enable ? Jump_Address[1] : 1'bz;  // Controlled_Buffer controlled_buffer_3
  Decoder decoder_3 (.out0(decoder_3_out0), .out1(decoder_3_out1), .sel(controlled_buffer_3_out));  // open: en
  and and_3 (and_3_out, Enable, out_8);
  assign controlled_buffer_4_out = Jump_Enable ? Jump_Address[0] : 1'bz;  // Controlled_Buffer controlled_buffer_4
  J_K_Flip_Flop #(.trigger("falling")) j_k_ff_3 (
    .J(1'b1), .clk(and_3_out), .K(1'b1), .Q(out_7), .preset(decoder_3_out1), .reset(decoder_3_out0));  // open: Qn, en
  Decoder decoder_4 (.out0(decoder_4_out0), .out1(decoder_4_out1), .sel(controlled_buffer_4_out));  // open: en
  J_K_Flip_Flop #(.trigger("falling")) j_k_ff_4 (
    .J(1'b1), .clk(and_4_out), .K(1'b1), .Q(out_8), .preset(decoder_4_out1), .reset(decoder_4_out0));  // open: Qn, en
  and and_4 (and_4_out, Enable, CLK);
endmodule

module Program_1___Add (
  input  CLK,
  input  [3:0] Read_Address,
  output _0,
  output out_4,
  output out_5,
  output out_6,
  output out_7,
  output out_8,
  output out_9,
  output _7,
  output _0___Halt_Program,
  output _1___ALU_Register_A_Write,
  output _2___ALU_Register_B_Write,
  output _3___ALU_Enable,
  output _4___ALU_Subtract
);

  wire decoder_1_out1, decoder_1_out2, decoder_1_out3, decoder_1_out4;
  wire [3:0] read_only_mem_1_output;

  Decoder #(.select(4)) decoder_1 (
    .out1(decoder_1_out1), .out2(decoder_1_out2), .out3(decoder_1_out3), .out4(decoder_1_out4),
    .sel(Read_Address));  // open: out0, out5, out6, out7, out8, out9, out10, out11, out12, out13, out14, out15, en
  Read_Only_Mem read_only_mem_1 (
    .CLK(CLK), .OpCode(4'b0001), .Buffer_CNTL(decoder_1_out1), .Output(read_only_mem_1_output));
  Read_Only_Data read_only_data_1 (
    .CLK(CLK), .Data(8'h4), .Buffer_CNTL(decoder_1_out1),
    .Output({_7, out_9, out_8, out_7, out_6, out_5, out_4, _0}));
  Read_Only_Mem read_only_mem_2 (
    .CLK(CLK), .OpCode(4'b0010), .Buffer_CNTL(decoder_1_out2), .Output(read_only_mem_1_output));
  Read_Only_Data read_only_data_2 (
    .CLK(CLK), .Data(8'h10), .Buffer_CNTL(decoder_1_out2),
    .Output({_7, out_9, out_8, out_7, out_6, out_5, out_4, _0}));
  Read_Only_Mem read_only_mem_3 (
    .CLK(CLK), .OpCode(4'b0011), .Buffer_CNTL(decoder_1_out3), .Output(read_only_mem_1_output));
  Read_Only_Mem read_only_mem_4 (
    .CLK(CLK), .OpCode(4'b0000), .Buffer_CNTL(decoder_1_out4), .Output(read_only_mem_1_output));
  Decoder #(.select(4)) decoder_2 (
    .out0(_0___Halt_Program), .out1(_1___ALU_Register_A_Write), .out2(_2___ALU_Register_B_Write),
    .out3(_3___ALU_Enable), .out4(_4___ALU_Subtract), .sel(read_only_mem_1_output));  // open: out5, out6, out7, out8, out9, out10, out11, out12, out13, out14, out15, en
  Pull_Resistor pull_resistor_1 (.node(_0___Halt_Program));
  Pull_Resistor pull_resistor_2 (.node(_1___ALU_Register_A_Write));
  Pull_Resistor pull_resistor_3 ();  // open: node
  Pull_Resistor pull_resistor_4 (.node(_2___ALU_Register_B_Write));
  Pull_Resistor pull_resistor_5 (.node(_3___ALU_Enable));
  Pull_Resistor pull_resistor_6 (.node(_4___ALU_Subtract));
  // NOT_Gate not_1 is placed but not wired

  // Notes on the sheet:
  //   0 : Halt Program
  //   1 :Enable Write To ALU Register A
  //   2 :Enable Write To ALU Register B
  //   3 : Enable ALU to BUS
endmodule

module Read_Only_Mem (
  input  CLK,
  input  [3:0] OpCode,
  input  Buffer_CNTL,
  output [3:0] Output
);

  wire [3:0] register_1_q;

  Register #(.width(4)) register_1 (.D(OpCode), .Q(register_1_q), .clk(CLK));  // open: en, clr
  assign Output = Buffer_CNTL ? register_1_q : 4'bz;  // Controlled_Buffer controlled_buffer_1
endmodule

module Read_Only_Data (
  input  CLK,
  input  [7:0] Data,
  input  Buffer_CNTL,
  output [7:0] Output
);

  wire [7:0] register_1_q;

  Register register_1 (.D(Data), .Q(register_1_q), .clk(CLK));  // open: en, clr
  assign Output = Buffer_CNTL ? register_1_q : 8'bz;  // Controlled_Buffer controlled_buffer_1
endmodule

module Program_2___Add_Loop (
  input  CLK,
  input  [3:0] Read_Address,
  output _0,
  output out_4,
  output out_5,
  output out_6,
  output out_7,
  output out_8,
  output out_9,
  output _7,
  output _0___Halt_Program,
  output _1___Write_ALU_Register_A,
  output _2___Write_ALU_Register_B,
  output _3___ALU_Enable,
  output _4___ALU_Subtract
);

  wire decoder_1_out1, decoder_1_out2, decoder_1_out3, decoder_1_out4, decoder_1_out5, decoder_1_out6,
       decoder_2_out0, decoder_2_out1, decoder_2_out2, decoder_2_out3, decoder_2_out4, decoder_3_out0,
       decoder_3_out1, decoder_3_out2, decoder_3_out3, decoder_3_out4;
  wire [3:0] read_only_mem_1_output, read_only_mem_4_output;

  Decoder #(.select(4)) decoder_1 (
    .out1(decoder_1_out1), .out2(decoder_1_out2), .out3(decoder_1_out3), .out4(decoder_1_out4),
    .out5(decoder_1_out5), .out6(decoder_1_out6), .sel(Read_Address));  // open: out0, out7, out8, out9, out10, out11, out12, out13, out14, out15, en
  Read_Only_Mem read_only_mem_1 (
    .CLK(CLK), .OpCode(4'b0001), .Buffer_CNTL(decoder_1_out1), .Output(read_only_mem_1_output));
  Read_Only_Data read_only_data_1 (
    .CLK(CLK), .Data(8'h5), .Buffer_CNTL(decoder_1_out1),
    .Output({_7, out_9, out_8, out_7, out_6, out_5, out_4, _0}));
  Read_Only_Mem read_only_mem_2 (
    .CLK(CLK), .OpCode(4'b0010), .Buffer_CNTL(decoder_1_out2), .Output(read_only_mem_1_output));
  Read_Only_Data read_only_data_2 (
    .CLK(CLK), .Data(8'h1), .Buffer_CNTL(decoder_1_out2),
    .Output({_7, out_9, out_8, out_7, out_6, out_5, out_4, _0}));
  Read_Only_Mem read_only_mem_3 (
    .CLK(CLK), .OpCode(4'b0011), .Buffer_CNTL(decoder_1_out3), .Output(read_only_mem_1_output));
  Read_Only_Mem read_only_mem_4 (
    .CLK(CLK), .OpCode(4'b0001), .Buffer_CNTL(decoder_1_out3), .Output(read_only_mem_4_output));
  Read_Only_Mem read_only_mem_5 (
    .CLK(CLK), .OpCode(4'b0011), .Buffer_CNTL(decoder_1_out4), .Output(read_only_mem_1_output));
  Read_Only_Mem read_only_mem_6 (
    .CLK(CLK), .OpCode(4'b0001), .Buffer_CNTL(decoder_1_out4), .Output(read_only_mem_4_output));
  Read_Only_Mem read_only_mem_7 (
    .CLK(CLK), .OpCode(4'b0011), .Buffer_CNTL(decoder_1_out5), .Output(read_only_mem_1_output));
  Read_Only_Mem read_only_mem_8 (
    .CLK(CLK), .OpCode(4'b0001), .Buffer_CNTL(decoder_1_out5), .Output(read_only_mem_4_output));
  Read_Only_Mem read_only_mem_9 (
    .CLK(CLK), .OpCode(4'b0000), .Buffer_CNTL(decoder_1_out6), .Output(read_only_mem_1_output));
  Read_Only_Mem read_only_mem_10 (
    .CLK(CLK), .OpCode(4'b0011), .Buffer_CNTL(decoder_1_out6), .Output(read_only_mem_4_output));
  Decoder #(.select(4)) decoder_2 (
    .out0(decoder_2_out0), .out1(decoder_2_out1), .out2(decoder_2_out2), .out3(decoder_2_out3),
    .out4(decoder_2_out4), .sel(read_only_mem_4_output));  // open: out5, out6, out7, out8, out9, out10, out11, out12, out13, out14, out15, en
  Pull_Resistor pull_resistor_1 ();  // open: node
  Decoder #(.select(4)) decoder_3 (
    .out0(decoder_3_out0), .out1(decoder_3_out1), .out2(decoder_3_out2), .out3(decoder_3_out3),
    .out4(decoder_3_out4), .sel(read_only_mem_1_output));  // open: out5, out6, out7, out8, out9, out10, out11, out12, out13, out14, out15, en
  Pull_Resistor pull_resistor_2 (.node(decoder_3_out0));
  Pull_Resistor pull_resistor_3 (.node(decoder_2_out0));
  Pull_Resistor pull_resistor_4 (.node(decoder_3_out1));
  Pull_Resistor pull_resistor_5 (.node(decoder_2_out1));
  Pull_Resistor pull_resistor_6 (.node(decoder_3_out2));
  Pull_Resistor pull_resistor_7 (.node(decoder_2_out2));
  Pull_Resistor pull_resistor_8 (.node(decoder_3_out3));
  Pull_Resistor pull_resistor_9 (.node(decoder_2_out3));
  Pull_Resistor pull_resistor_10 (.node(decoder_3_out4));
  Pull_Resistor pull_resistor_11 (.node(decoder_2_out4));
  Pull_Resistor pull_resistor_12 ();  // open: node
  Pull_Resistor pull_resistor_13 ();  // open: node
  or or_1 (_0___Halt_Program, decoder_3_out0, decoder_2_out0);
  or or_2 (_1___Write_ALU_Register_A, decoder_3_out1, decoder_2_out1);
  or or_3 (_2___Write_ALU_Register_B, decoder_3_out2, decoder_2_out2);
  or or_4 (_3___ALU_Enable, decoder_3_out3, decoder_2_out3);
  or or_5 (_4___ALU_Subtract, decoder_3_out4, decoder_2_out4);
  // NOT_Gate not_1 is placed but not wired

  // Notes on the sheet:
  //   Start Prog Here
  //   Line 1
  //   Line 2
  //   0 : Halt Program
  //   1 :Enable Write To ALU Register A
  //   2 :Enable Write To ALU Register B
  //   3 : Enable ALU to BUS
  //   Line 2
  //   Line 1
endmodule
